# Fritzing sketch Arduino-Nano-433MHz-DHT22-YL69_Wiring (saved by Fritzing 0.9.3b)
circuit board: 8.46667cm x 5.64444cm

parts:
  Resistor = Resistor [tolerance=±5% resistance=220 package=THT]
  DHT22 = Humidity and Temperature Sensor RHT03
  Transmitter_433MHz = FS1000A - 433Mhz RF Transmitter [package=THT]
  Soil_Moisture_Sensor = Soil Moisture Sensor
  Arduino_Nano_V3 = Arduino Nano (Rev3.0)
  Transistor = NPN-Transistor [package="SOT-23 [SMD]"]

nets:
  VCC: Resistor.Pin_0, DHT22.Vcc, Transmitter_433MHz.VCC, Arduino_Nano_V3.D11/MOSI, Arduino_Nano_V3.5V, Transistor.1
  N1: Resistor.Pin_1, DHT22.Data-signal, Arduino_Nano_V3.D4
  GND: DHT22.GND_2, Transmitter_433MHz.GND, Soil_Moisture_Sensor.GND, Arduino_Nano_V3.GND, Arduino_Nano_V3.D10, Arduino_Nano_V3.A0, Arduino_Nano_V3.AREF
  N2: Transmitter_433MHz.DATA, Arduino_Nano_V3.D12/MISO
  N3: Soil_Moisture_Sensor.SIG, Arduino_Nano_V3.A1
  N4: Soil_Moisture_Sensor.VCC, Transistor.2
  N5: Arduino_Nano_V3.D2, Transistor.0

custom parts:
  FS1000A - 433Mhz RF Transmitter: This is 433Mhz RF transmitter with receiver kit for Arduino ARM MCU wireless Application environment: Remote control switch, receiver module, motorcycles, automobile anti-theft products, home security products, electric doors, shutter doors, windows, remote control socket, remote control LED, remote audio remote control electric doors, garage door remote control, remote control retractable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
